# Fritzing sketch Slave Fritzing (saved by Fritzing 0.9.3b)
breadboards: 1

parts:
  Componente1 = Arduino Uno (Rev3)
  LED1 = LED - 3mm [color="Red (633nm)" package="3 mm [THT]"]
  R1 = Resistor [tolerance=±5% resistance=220 package="2010 [SMD]"]
  Componente2 = NRF24L01+ Breakout Board

nets:
  N1: Componente1.D9_PWM, Componente2.CE
  N2: Componente1.D10_PWM/SS, Componente2.CS
  N3: Componente1.D11_PWM/MOSI, Componente2.MOSI
  N4: Componente1.D12/MISO, Componente2.MISO
  N5: Componente1.D13/SCK, Componente2.SCK
  N6: Componente1.D3_PWM, R1.Pin_1
  3V3: Componente1.3V3, Componente2.VCC
  GND: Componente1.GND, LED1.cathode, Componente2.GND
  N7: LED1.anode, R1.Pin_0
